# Fritzing sketch Schematics (saved by Fritzing 0.9.4)
circuit board: 8.46667cm x 5.64444cm
breadboards: 1

parts:
  Nano_33_IoT = Arduino Nano (Rev3.0) (ICSP)
  R1 = Resistor [tolerance=±5% resistance=2.2k package="2010 [SMD]"]
  R2 = Resistor [tolerance=±5% resistance=3.3k package="2010 [SMD]"]
  S1 = Square Pushbutton
  S2 = Square Pushbutton
  R3 = Resistor [tolerance=±5% resistance=330 package="2010 [SMD]"]
  R4 = Resistor [tolerance=±5% resistance=330 package="2010 [SMD]"]
  R5 = Resistor [tolerance=±5% resistance=330 package="2010 [SMD]"]
  LED1 = LED - 5mm [color="Red (633nm)" package="5 mm [THT]"]
  LED2 = LED - 5mm [color="Red (633nm)" package="5 mm [THT]"]
  LED3 = LED - 5mm [color="Red (633nm)" package="5 mm [THT]"]
  HC-SR04_Sensor_1 = HC-SR04 Ultrasonic Distance Sensor
  RHT1 = Humidity and Temperature Sensor RHT03 [part_number=DHT11]

nets:
  GND: Nano_33_IoT.GND, R2.Pin_0, S1.leg0, S2.leg0, LED1.cathode, LED2.cathode, LED3.cathode, HC-SR04_Sensor_1.GND, RHT1.GND_2
  N1: Nano_33_IoT.D2, S1.leg1
  N2: Nano_33_IoT.D3, S2.leg1
  N3: Nano_33_IoT.D4, HC-SR04_Sensor_1.TRIG
  N4: Nano_33_IoT.D5, R1.Pin_0, R2.Pin_1
  N5: Nano_33_IoT.D6, R5.Pin_0
  N6: Nano_33_IoT.D7, R4.Pin_0
  N7: Nano_33_IoT.D8, R3.Pin_0
  N8: Nano_33_IoT.D10, RHT1.Data-signal
  5V: Nano_33_IoT.5V, HC-SR04_Sensor_1.VCC
  3V3: Nano_33_IoT.3V3, RHT1.Vcc
  N9: R1.Pin_1, HC-SR04_Sensor_1.ECHO
  N10: R3.Pin_1, LED1.anode
  N11: R4.Pin_1, LED3.anode
  N12: R5.Pin_1, LED2.anode
